// Logisim project TrabalhoSD.circ as structural Verilog
module main (
  input  in_1,
  input  [3:0] X,
  input  [3:0] Y,
  input  [1:0] Seletor,
  output [3:0] Z,
  output Negativo,
  output Zero,
  output Cout,
  output OverFlow
);

  wire incremento_1_cout, incremento_1_negativo, incremento_1_overflow, incremento_1_zero,
       somador4bits_1_cout, somador4bits_1_negativo, somador4bits_1_overflow, somador4bits_1_zero,
       subtrator4bits_1_cout, subtrator4bits_1_negativo, subtrator4bits_1_overflow, subtrator4bits_1_zero,
       trocadesinal_1_cout, trocadesinal_1_negativo, trocadesinal_1_overflow, trocadesinal_1_zero;
  wire [3:0] incremento_1_z, somador4bits_1_z, subtrator4bits_1_z, trocadesinal_1_z;

  Somador4Bits somador4bits_1 (
    .Cin(in_1), .X(X), .Y(Y), .Z(somador4bits_1_z), .Negativo(somador4bits_1_negativo),
    .Zero(somador4bits_1_zero), .Cout(somador4bits_1_cout), .OverFlow(somador4bits_1_overflow));
  Subtrator4Bits subtrator4bits_1 (
    .X(X), .Y(Y), .Z(subtrator4bits_1_z), .Negativo(subtrator4bits_1_negativo), .Zero(subtrator4bits_1_zero),
    .Cout(subtrator4bits_1_cout), .OverFlow(subtrator4bits_1_overflow));
  Incremento incremento_1 (
    .X(X), .Z(incremento_1_z), .Negativo(incremento_1_negativo), .Zero(incremento_1_zero),
    .Cout(incremento_1_cout), .OverFlow(incremento_1_overflow));
  TrocaDeSinal trocadesinal_1 (
    .X(X), .Z(trocadesinal_1_z), .Negativo(trocadesinal_1_negativo), .Zero(trocadesinal_1_zero),
    .Cout(trocadesinal_1_cout), .OverFlow(trocadesinal_1_overflow));
  Multiplexer #(.select(2), .width(4)) multiplexer_1 (
    .in0(somador4bits_1_z), .in1(incremento_1_z), .in2(subtrator4bits_1_z), .in3(trocadesinal_1_z), .out(Z),
    .sel(Seletor));
  Multiplexer #(.select(2)) multiplexer_2 (
    .in0(somador4bits_1_negativo), .in1(incremento_1_negativo), .in2(subtrator4bits_1_negativo),
    .in3(trocadesinal_1_negativo), .out(Negativo), .sel(Seletor));
  Multiplexer #(.select(2)) multiplexer_3 (
    .in0(somador4bits_1_zero), .in1(incremento_1_zero), .in2(subtrator4bits_1_zero),
    .in3(trocadesinal_1_zero), .out(Zero), .sel(Seletor));
  Multiplexer #(.select(2)) multiplexer_4 (
    .in0(somador4bits_1_cout), .in1(incremento_1_cout), .in2(subtrator4bits_1_cout),
    .in3(trocadesinal_1_cout), .out(Cout), .sel(Seletor));
  Multiplexer #(.select(2)) multiplexer_5 (
    .in0(somador4bits_1_overflow), .in1(incremento_1_overflow), .in2(subtrator4bits_1_overflow),
    .in3(trocadesinal_1_overflow), .out(OverFlow), .sel(Seletor));
endmodule

module Somador (
  input  Cin,
  input  X,
  input  Y,
  output Z,
  output Cout
);

  wire and_1_out, and_2_out, xor_1_out;

  xor xor_1 (xor_1_out, X, Y);
  and and_1 (and_1_out, xor_1_out, Cin);
  and and_2 (and_2_out, X, Y);
  xor xor_2 (Z, xor_1_out, Cin);
  or or_1 (Cout, and_1_out, and_2_out);
endmodule

module Subtrator4Bits (
  input  [3:0] X,
  input  [3:0] Y,
  output [3:0] Z,
  output Negativo,
  output Zero,
  output Cout,
  output OverFlow
);

  wire [3:0] not_1_out;

  assign not_1_out = ~Y;  // NOT_Gate not_1, 4 bits wide
  Somador4Bits somador4bits_1 (
    .Cin(1'b1), .X(X), .Y(not_1_out), .Z(Z), .Negativo(Negativo), .Zero(Zero), .Cout(Cout),
    .OverFlow(OverFlow));
endmodule

module Somador4Bits (
  input  Cin,
  input  [3:0] X,
  input  [3:0] Y,
  output [3:0] Z,
  output Negativo,
  output Zero,
  output Cout,
  output OverFlow
);

  wire and_2_out, and_3_out, not_1_out, not_2_out, not_3_out, not_4_out, somador_1_cout, somador_2_cout,
       somador_3_cout;

  Somador somador_1 (.Cin(Cin), .X(X[0]), .Y(Y[0]), .Z(Z[0]), .Cout(somador_1_cout));
  Somador somador_2 (.Cin(somador_1_cout), .X(X[1]), .Y(Y[1]), .Z(Z[1]), .Cout(somador_2_cout));
  Somador somador_3 (.Cin(somador_2_cout), .X(X[2]), .Y(Y[2]), .Z(Z[2]), .Cout(somador_3_cout));
  Somador somador_4 (.Cin(somador_3_cout), .X(X[3]), .Y(Y[3]), .Z(Negativo), .Cout(Cout));
  not not_1 (not_1_out, Z[0]);
  not not_2 (not_2_out, Z[1]);
  not not_3 (not_3_out, Z[2]);
  not not_4 (not_4_out, Negativo);
  and and_1 (Zero, not_1_out, not_2_out, not_3_out, not_4_out);
  and and_2 (and_2_out, ~Negativo, X[3], Y[3]);  // AND_Gate
  and and_3 (and_3_out, Negativo, ~X[3], ~Y[3]);  // AND_Gate
  or or_1 (OverFlow, and_2_out, and_3_out);

  assign Z[3] = Negativo;
endmodule

module Incremento (
  input  [3:0] X,
  output [3:0] Z,
  output Negativo,
  output Zero,
  output Cout,
  output OverFlow
);

  Somador4Bits somador4bits_1 (
    .Cin(1'b0), .X(X), .Y(4'b0001), .Z(Z), .Negativo(Negativo), .Zero(Zero), .Cout(Cout), .OverFlow(OverFlow));
endmodule

module TrocaDeSinal (
  input  [3:0] X,
  output [3:0] Z,
  output Negativo,
  output Zero,
  output Cout,
  output OverFlow
);

  wire [3:0] not_1_out;

  assign not_1_out = ~X;  // NOT_Gate not_1, 4 bits wide
  Somador4Bits somador4bits_1 (
    .Cin(1'b0), .X(not_1_out), .Y(4'b0001), .Z(Z), .Negativo(Negativo), .Zero(Zero), .Cout(Cout),
    .OverFlow(OverFlow));
endmodule

module ShifterLeft (
  input  in_1
);

  // Somador somador_1: pin names not known; wires that end beside it: in_1
endmodule

module TesteVhdl (
  input  in_1,
  input  in_2,
  input  in_3,
  input  [3:0] in_4,
  input  [3:0] in_5,
  input  [2:0] in_6,
  output out_7,
  output out_8,
  output [3:0] out_9,
  output out_10,
  output out_11,
  output out_12,
  output out_13
);

  wire ha_1_cout, ha_1_s, ha_2_cout;

  HA ha_1 (.A(in_1), .B(in_2), .S(ha_1_s), .Cout(ha_1_cout));
  ULA ula_1 (
    .a(in_4), .b(in_5), .seletor(in_6[1:0]), .resultado(out_9), .ovf(out_10), .zero(out_11), .Neg(out_12),
    .cout(out_13));
  HA ha_2 (.A(ha_1_s), .B(in_3), .S(out_7), .Cout(ha_2_cout));
  or or_1 (out_8, ha_2_cout, ha_1_cout);
  // Pins of 2 and 3 bits meet at in_6
endmodule

module Decremento (
  input  [3:0] X,
  output [3:0] Z,
  output Negativo,
  output Zero,
  output Cout,
  output OverFlow
);

  wire [3:0] not_1_out;

  not not_1 (not_1_out[0], 1'b1);
  not not_2 (not_1_out[1], 1'b0);
  not not_3 (not_1_out[2], 1'b0);
  not not_4 (not_1_out[3], 1'b0);
  Somador4Bits somador4bits_1 (
    .Cin(1'b1), .X(X), .Y(not_1_out), .Z(Z), .Negativo(Negativo), .Zero(Zero), .Cout(Cout),
    .OverFlow(OverFlow));
endmodule

module MultiplicaPor2 (
  input  [3:0] X,
  output [3:0] Z,
  output Negativo,
  output Zero,
  output Cout,
  output OverFlow
);

  Somador4Bits somador4bits_1 (
    .Cin(1'b0), .X(X), .Y(X), .Z(Z), .Negativo(Negativo), .Zero(Zero), .Cout(Cout), .OverFlow(OverFlow));
endmodule

// VHDL entity HA, as the project stores it:
LIBRARY ieee;
USE ieee.std_logic_1164.all;


ENTITY HA IS

    PORT (

        A      : IN  std_logic;
        B      : IN  std_logic;
        
        S      : OUT std_logic;
        Cout   : OUT std_logic
    
    );

END HA;


ARCHITECTURE Behavioral OF HA IS

BEGIN

    S <= A XOR B;
    Cout <= A AND B;

END Behavioral;

// VHDL entity FA, as the project stores it:
LIBRARY ieee;
USE ieee.std_logic_1164.all;


ENTITY FA IS

    PORT (

        a      : IN  std_logic;
        b      : IN  std_logic;
        cin      : IN  std_logic;


        s      : OUT std_logic;
        cout   : OUT std_logic
    
    );

END FA;


ARCHITECTURE Structural OF FA IS

    COMPONENT HA 

        PORT (

            A      : IN  std_logic;
            B      : IN  std_logic;

            S      : OUT std_logic;
            Cout   : OUT std_logic

        );

    END COMPONENT;

    SIGNAL somaHA1, coutHA1, coutHA2: std_logic;

    BEGIN

        HA1: HA PORT MAP (

            a,
            b,
            somaHA1,
            coutHA1
        );
        
        HA2: HA PORT MAP (

            somaHA1,
            cin,
            s,
            coutHA2
        );

        cout <= coutHA1 OR coutHA2;

END Structural;

// VHDL entity ULA, as the project stores it:
library ieee;
use ieee.std_logic_1164.all;

ENTITY ULA IS
    PORT (
    
        a, b            :       in std_logic_vector(3 DOWNTO 0);
        seletor         :       in std_logic_vector(1 DOWNTO 0);
        --seletor       :       in std_logic_vector(2 DOWNTO 0);

        resultado       :       out std_logic_vector(3 DOWNTO 0);

        ovf             :       out std_logic;
        zero            :       out std_logic;
        Neg             :       out std_logic;
        cout            :       out std_logic
  
    );
END ULA;

ARCHiTECTURE Behavioral OF ULA IS
  
    FUNCTION HA(a, b: std_logic) RETURN std_logic_vector IS 
    
        VARIABLE sum, cout: std_logic;
  
        BEGIN
    
            sum := a XOR b;
            cout := a AND b;
            return (sum, cout);
  
    END FUNCTION;

    FUNCTION FA(a, b, c: std_logic) RETURN std_logic_vector IS 
    
        VARIABLE sum, cout                  :       std_logic;
        VARIABLE sumHA1,coutHA1,coutHA2     :       std_logic;

        BEGIN

            (sumHA1,coutHA1)    :=   HA(a,b);
            (sum,coutHA2)       :=   HA(sumHA1,c);
            cout                :=   coutHA1 OR coutHA2;

            RETURN (sum, cout);
    
    END FUNCTION;

    FUNCTION somador4Bits(a,b : std_logic_vector) RETURN std_logic_vector IS

        VARIABLE sum, cout                  :      std_logic_vector(3 DOWNTO 0);

        BEGIN

            (sum(0), cout(0)) := FA(a(0), b(0), '0');
            (sum(1), cout(1)) := FA(a(1), b(1), cout(0));
            (sum(2), cout(2)) := FA(a(2), b(2), cout(1));
            (sum(3), cout(3)) := FA(a(3), b(3), cout(2));

            RETURN (sum(3),sum(2),sum(1),sum(0),cout(3),cout(2),cout(1),cout(0));

    END FUNCTION;

    FUNCTION subtrator4Bits(a,b : std_logic_vector) RETURN std_logic_vector IS

        VARIABLE sum, cout                  :      std_logic_vector(3 DOWNTO 0);

        BEGIN

            (sum(0), cout(0)) := FA(a(0), (NOT b(0)), '1');
            (sum(1), cout(1)) := FA(a(1), (NOT b(1)), cout(0));
            (sum(2), cout(2)) := FA(a(2), (NOT b(2)), cout(1));
            (sum(3), cout(3)) := FA(a(3), (NOT b(3)), cout(2));

            RETURN (sum(3),sum(2),sum(1),sum(0),cout(3),cout(2),cout(1),cout(0));

    END FUNCTION;

    FUNCTION trocaDeSinal(a,b : std_logic_vector) RETURN std_logic_vector IS

        VARIABLE sum, cout                  :      std_logic_vector(3 DOWNTO 0);

        BEGIN

            (sum(0), cout(0)) := FA('0', (NOT b(0)), '1');
            (sum(1), cout(1)) := FA('0', (NOT b(1)), cout(0));
            (sum(2), cout(2)) := FA('0', (NOT b(2)), cout(1));
            (sum(3), cout(3)) := FA('0', (NOT b(3)), cout(2));

            RETURN (sum(3),sum(2),sum(1),sum(0),cout(3),cout(2),cout(1),cout(0));

    END FUNCTION;

    FUNCTION incrementoDe1(a,b : std_logic_vector) RETURN std_logic_vector IS

        VARIABLE sum, cout                  :      std_logic_vector(3 DOWNTO 0);

        BEGIN

            (sum(0), cout(0)) := FA(a(0), '1', '0');
            (sum(1), cout(1)) := FA(a(1), '0', cout(0));
            (sum(2), cout(2)) := FA(a(2), '0', cout(1));
            (sum(3), cout(3)) := FA(a(3), '0', cout(2));

            RETURN (sum(3),sum(2),sum(1),sum(0),cout(3),cout(2),cout(1),cout(0));

    END FUNCTION;

    -- SOMA
    SIGNAL soma, carryoutSOMA : std_logic_vector(3 DOWNTO 0);

    -- SUBTRAÇÃO
    SIGNAL sub, carryoutSUB : std_logic_vector(3 DOWNTO 0);

    -- INCREMENTO DE 1
    SIGNAL inc, carryoutINC : std_logic_vector(3 DOWNTO 0);

    -- TROCA DE SINAL
    SIGNAL tds, carryoutTDS : std_logic_vector(3 DOWNTO 0);



    BEGIN

    (soma(3),soma(2),soma(1),soma(0),carryoutSOMA(3),carryoutSOMA(2),carryoutSOMA(1),carryoutSOMA(0)) <= somador4Bits(a,b);
    (sub(3),sub(2),sub(1),sub(0),carryoutSUB(3),carryoutSUB(2),carryoutSUB(1),carryoutSUB(0)) <= subtrator4Bits(a,b);
    (inc(3),inc(2),inc(1),inc(0),carryoutINC(3),carryoutINC(2),carryoutINC(1),carryoutINC(0)) <= incrementoDe1(a,b);
    (tds(3),tds(2),tds(1),tds(0),carryoutTDS(3),carryoutTDS(2),carryoutTDS(1),carryoutTDS(0)) <= trocaDeSinal(a,b);


    resultado   <=  soma    WHEN    seletor <= "00"  ELSE
                    sub     WHEN    seletor <= "01"  ELSE
                    inc     WHEN    seletor <= "10"  ELSE
                    tds     WHEN    seletor <= "11";

    cout        <=  carryoutSOMA(3)    WHEN    seletor <= "00"  ELSE
                    carryoutSUB(3)     WHEN    seletor <= "01"  ELSE
                    carryoutINC(3)     WHEN    seletor <= "10"  ELSE
                    carryoutTDS(3)     WHEN    seletor <= "11";

END Behavioral;

// VHDL entity FullAdder, as the project stores it:
library ieee;
use ieee.std_logic_1164.all;

ENTITY FullAdder IS
  PORT (
    a, b, cin: in std_logic;
    sum, cout: out std_logic
  );
END FullAdder;

ARCHiTECTURE Behavioral OF FullAdder IS
  
    FUNCTION HA(a, b: std_logic) RETURN std_logic_vector IS 
    
        VARIABLE sum, cout: std_logic;
  
        BEGIN
    
            sum := a XOR b;
            cout := a AND b;
            return (sum, cout);
  
    END FUNCTION;

    FUNCTION FA(a, b, c: std_logic) RETURN std_logic_vector IS 
    
        VARIABLE sum, cout  :       std_logic;
        VARIABLE sumHA1,coutHA1,coutHA2     :       std_logic;

        BEGIN

            (sumHA1,coutHA1)    :=   HA(a,b);
            (sum,coutHA2)       :=   HA(sumHA1,c);
            cout                :=   coutHA1 OR coutHA2;

            RETURN (sum, cout);
    
    END FUNCTION;

    BEGIN

    (sum,cout) <= FA(a,b,cin);


END Behavioral;

// VHDL entity FourBitAdder, as the project stores it:
library ieee;
use ieee.std_logic_1164.all;

ENTITY FourBitAdder IS
  PORT (
    a, b    :   in std_logic_vector(3 DOWNTO 0);
    sum     :   out std_logic_vector(3 DOWNTO 0); 
    cout    :   out std_logic
  );
END FourBitAdder;

ARCHiTECTURE Behavioral OF FourBitAdder IS
  
    FUNCTION HA(a, b: std_logic) RETURN std_logic_vector IS 
    
        VARIABLE sum, cout: std_logic;
  
        BEGIN
    
            sum := a XOR b;
            cout := a AND b;
            return (sum, cout);
  
    END FUNCTION;

    FUNCTION FA(a, b, c: std_logic) RETURN std_logic_vector IS 
    
        VARIABLE sum, cout                  :       std_logic;
        VARIABLE sumHA1,coutHA1,coutHA2     :       std_logic;

        BEGIN

            (sumHA1,coutHA1)    :=   HA(a,b);
            (sum,coutHA2)       :=   HA(sumHA1,c);
            cout                :=   coutHA1 OR coutHA2;

            RETURN (sum, cout);
    
    END FUNCTION;

    FUNCTION somador4Bits(a,b : std_logic_vector) RETURN std_logic_vector IS

        VARIABLE sum, cout                  :      std_logic_vector(3 DOWNTO 0);

        BEGIN

            (sum(0), cout(0)) := FA(a(0), b(0), '0');
            (sum(1), cout(1)) := FA(a(1), b(1), cout(0));
            (sum(2), cout(2)) := FA(a(2), b(2), cout(1));
            (sum(3), cout(3)) := FA(a(3), b(3), cout(2));

            RETURN (sum(3),sum(2),sum(1),sum(0),cout(3),cout(2),cout(1),cout(0));

    END FUNCTION;

    SIGNAL carryout : std_logic_vector(3 DOWNTO 0);

    BEGIN

    (sum(3),sum(2),sum(1),sum(0),carryout(3),carryout(2),carryout(1),carryout(0)) <= somador4Bits(a,b);
    cout <= carryout(3);

END Behavioral;
